# Fritzing sketch Quant_Mo_Arduino (saved by Fritzing 0.9.3b)
circuit board: 4.25344cm x 5.40464cm
breadboards: 1

parts:
  Part1 = Arduino Nano (Rev3.0)
  Part2 = NRF24L01+ Breakout Board
  R1 = Photocell (LDR) [package=THT]
  R2 = Resistor [tolerance=±5% resistance=1k package=THT]
  R3 = Photocell (LDR) [package=THT]
  R5 = Photocell (LDR) [package=THT]
  R6 = Resistor [tolerance=±5% resistance=1k package=THT]
  R7 = Photocell (LDR) [package=THT]
  R8 = Resistor [tolerance=±5% resistance=1k package=THT]
  R4 = Resistor [tolerance=±5% resistance=1k package=THT]

nets:
  GND: Part1.GND, Part2.GND, R2.Pin_1, R6.Pin_1, R8.Pin_1, R4.Pin_1
  N1: Part1.D9, Part2.CE
  N2: Part1.D10, Part2.CS
  N3: Part1.D11/MOSI, Part2.MOSI
  N4: Part1.D12/MISO, Part2.MISO
  N5: Part1.5V, R1.pin_0, R3.pin_0, R5.pin_0, R7.pin_0
  N6: Part1.A4, R7.pin_1, R8.Pin_0
  N7: Part1.A3, R5.pin_1, R6.Pin_0
  N8: Part1.A2, R3.pin_1, R4.Pin_0
  N9: Part1.A1, R1.pin_1, R2.Pin_0
  3V3: Part1.3V3, Part2.VCC
  N10: Part1.D13/SCK, Part2.SCK
